// Logisim project makp2.circ as structural Verilog: 1 circuit, main circuit main
module main (
  input  in_1,
  input  in_2,
  input  in_3
);

  wire and_1_out, and_3_out, and_4_out, and_5_out, and_6_out, and_7_out, and_8_out, and_9_out, and_10_out,
       and_11_out, and_12_out, and_13_out, and_14_out, and_15_out, and_16_out, and_17_out, and_18_out,
       and_19_out, and_20_out, and_21_out, and_22_out, and_23_out, and_24_out, and_25_out, and_26_out,
       and_27_out, and_28_out, and_29_out, and_30_out, and_31_out, and_32_out, and_33_out, and_34_out,
       and_35_out, and_36_out, and_37_out, and_38_out, and_39_out, and_40_out, and_41_out, and_42_out,
       and_43_out, and_44_out, and_45_out, and_46_out, and_47_out, and_48_out, and_49_out, and_50_out,
       and_51_out, and_52_out, and_53_out, and_54_out, and_55_out, and_56_out, and_57_out, and_58_out,
       and_59_out, bit_extender_1_out, CLK, clock_1_out, comparator_1_eq, comparator_1_gt, comparator_1_lt,
       comparator_2_eq, comparator_2_gt, comparator_2_lt, demultiplexer_2_out0, demultiplexer_2_out2,
       demultiplexer_2_out3, demultiplexer_3_out0, demultiplexer_3_out1, demultiplexer_3_out4,
       demultiplexer_3_out5, demultiplexer_4_out0, demultiplexer_4_out1, demultiplexer_4_out2,
       demultiplexer_5_out0, demultiplexer_5_out1, demultiplexer_5_out2, demultiplexer_5_out3,
       demultiplexer_6_out0, demultiplexer_6_out1, demultiplexer_6_out2, demultiplexer_6_out3,
       demultiplexer_7_out1, demultiplexer_7_out2, demultiplexer_7_out3, demultiplexer_7_out4,
       demultiplexer_7_out5, demultiplexer_7_out6, demultiplexer_7_out7, demultiplexer_7_out8,
       demultiplexer_7_out9, demultiplexer_7_out10, demultiplexer_7_out11, demultiplexer_7_out12,
       demultiplexer_7_out13, demultiplexer_7_out14, demultiplexer_7_out15, demultiplexer_7_out16,
       demultiplexer_7_out17, demultiplexer_7_out18, demultiplexer_7_out19, demultiplexer_7_out20,
       demultiplexer_7_out21, demultiplexer_7_out22, demultiplexer_7_out23, demultiplexer_7_out24,
       demultiplexer_7_out25, demultiplexer_7_out26, demultiplexer_7_out27, demultiplexer_7_out28,
       demultiplexer_7_out29, demultiplexer_7_out30, demultiplexer_7_out31, keyboard_1_avail,
       multiplexer_2_out, not_1_out, not_2_out, not_3_out, not_4_out, not_5_out, not_6_out, not_7_out,
       or_1_out, or_2_out, or_3_out, or_4_out, or_5_out, or_6_out, or_7_out, or_8_out, or_9_out, or_10_out,
       or_12_out, or_13_out, or_14_out;
  wire [1:0] controlled_buffer_4_out, controlled_buffer_44_out, demultiplexer_1_out0, multiplexer_6_out;
  wire [2:0] controlled_buffer_32_out;
  wire [3:0] controlled_buffer_12_out;
  wire [4:0] bit_extender_2_out, controlled_buffer_1_out;
  wire [6:0] bit_extender_4_out, keyboard_1_data;
  wire [7:0] multiplexer_7_out, multiplexer_8_out, multiplexer_9_out, multiplexer_10_out,
       multiplexer_15_out_2, multiplexer_16_out, multiplexer_17_out, multiplexer_18_out, multiplexer_19_out,
       multiplexer_23_out, multiplexer_23_out_2, multiplexer_23_out_3, multiplexer_23_out_4, ram_1_dout,
       ram_2_dout, ram_3_dout, ram_4_dout;
  wire [11:0] controlled_buffer_10_out;
  wire [20:1] controlled_buffer_7_out;
  wire [21:0] adder_2_out, bit_extender_6_out, demultiplexer_1_out0_2, multiplexer_11_out,
       multiplexer_12_out, multiplexer_13_out;
  wire [21:10] controlled_buffer_8_out, controlled_buffer_9_out;
  wire [23:0] adder_1_out, bit_extender_3_out, demultiplexer_1_out1, multiplexer_3_out, multiplexer_4_out,
       multiplexer_15_out, register_1_q, subtractor_1_out, subtractor_2_out;
  wire [24:0] controlled_buffer_2_out, multiplexer_5_out;
  wire [24:5] controlled_buffer_6_out;
  wire [31:0] adder_3_out, and_60_out, bit_extender_8_out, bit_extender_9_out, bit_extender_10_out,
       bit_extender_11_out, bit_extender_12_out, bit_extender_13_out, bit_extender_14_out,
       bit_extender_15_out, bit_extender_16_out, bit_extender_17_out, bit_extender_18_out,
       bit_extender_19_out, controlled_buffer_63_out, multiplexer_1_out, multiplexer_14_out,
       multiplexer_20_out, multiplexer_21_out, multiplexer_22_out, or_11_out, RAM_OUT, shifter_1_out,
       shifter_2_out, shifter_3_out, subtractor_3_out, x1_q, x2_q, x3_q, x4_q, x5_q, x6_q, x7_q, x8_q, x9_q,
       x10_q, x11_q, x12_q, x13_q, x14_q, x15_q, x16_q, x17_q, x18_q, x19_q, x20_q, x21_q, x22_q, x23_q,
       x24_q, x25_q, x26_q, x27_q, x28_q, x29_q, x30_q, x31_q, xor_1_out;
  wire [31:5] bit_extender_2_out_2;

  or or_1 (or_1_out, and_13_out, and_1_out);
  Clock clock_1 (.out(clock_1_out));
  Subtractor #(.width(24)) subtractor_1 (.a(bit_extender_3_out), .b(24'h4), .out(subtractor_1_out));  // open: bin, bout
  or or_2 (or_2_out, or_1_out, and_50_out);
  not not_1 (not_1_out, CLK);
  Multiplexer #(.width(32)) multiplexer_1 (.in0({32{1'b0}}), .in1(RAM_OUT), .out(multiplexer_1_out), .sel(CLK));
  and and_1 (and_1_out, and_10_out, multiplexer_2_out);
  Multiplexer multiplexer_2 (.in0(1'b0), .in1(bit_extender_1_out), .out(multiplexer_2_out), .sel(and_10_out));
  Multiplexer #(.width(24)) multiplexer_3 (
    .in0(adder_1_out), .in1(multiplexer_15_out), .out(multiplexer_3_out), .sel(and_50_out));
  and and_2 (CLK, in_3, clock_1_out);
  and and_3 (and_3_out, ~and_5_out, ~and_6_out, ~and_7_out, ~and_8_out, ~and_11_out, ~and_12_out, ~and_13_out);  // AND_Gate
  Bit_Extender #(.in_width(32), .out_width(1), .\type ("input")) bit_extender_1 (
    .in({multiplexer_15_out_2, multiplexer_15_out}), .out(bit_extender_1_out));  // open: extend
  or or_3 (or_3_out, CLK, and_4_out);
  and and_4 (and_4_out, or_2_out, not_1_out);
  assign controlled_buffer_1_out = and_3_out ? {5{1'b0}} : 5'bz;  // Controlled_Buffer controlled_buffer_1
  Multiplexer #(.width(24)) multiplexer_4 (
    .in0(24'h4), .in1(subtractor_1_out), .out(multiplexer_4_out), .sel(or_1_out));
  Register #(.width(24)) register_1 (.D(multiplexer_3_out), .clk(or_3_out), .Q(register_1_q), .clr(in_1));  // open: en
  Adder #(.width(24)) adder_1 (.a(multiplexer_4_out), .b(register_1_q), .out(adder_1_out));  // open: cin, cout
  Subtractor #(.width(24)) subtractor_2 (.a(register_1_q), .b(24'h4), .out(subtractor_2_out));  // open: bin, bout
  or or_4 (or_4_out, and_7_out, and_9_out);
  and and_5 (and_5_out, multiplexer_1_out[0], multiplexer_1_out[1], ~multiplexer_1_out[2], ~multiplexer_1_out[3], multiplexer_1_out[4], multiplexer_1_out[5], ~multiplexer_1_out[6]);  // AND_Gate
  and and_6 (and_6_out, multiplexer_1_out[0], multiplexer_1_out[1], ~multiplexer_1_out[2], ~multiplexer_1_out[3], multiplexer_1_out[4], ~multiplexer_1_out[5], ~multiplexer_1_out[6]);  // AND_Gate
  and and_7 (and_7_out, multiplexer_1_out[0], multiplexer_1_out[1], ~multiplexer_1_out[2], ~multiplexer_1_out[3], ~multiplexer_1_out[4], ~multiplexer_1_out[5], ~multiplexer_1_out[6]);  // AND_Gate
  and and_8 (and_8_out, multiplexer_1_out[0], multiplexer_1_out[1], multiplexer_1_out[2], ~multiplexer_1_out[3], ~multiplexer_1_out[4], multiplexer_1_out[5], multiplexer_1_out[6]);  // AND_Gate
  and and_9 (and_9_out, multiplexer_1_out[0], multiplexer_1_out[1], ~multiplexer_1_out[2], ~multiplexer_1_out[3], ~multiplexer_1_out[4], multiplexer_1_out[5], ~multiplexer_1_out[6]);  // AND_Gate
  assign controlled_buffer_2_out = and_10_out ? multiplexer_1_out[31:7] : 25'bz;  // Controlled_Buffer controlled_buffer_2
  and and_10 (and_10_out, multiplexer_1_out[0], multiplexer_1_out[1], ~multiplexer_1_out[2], ~multiplexer_1_out[3], ~multiplexer_1_out[4], multiplexer_1_out[5], multiplexer_1_out[6]);  // AND_Gate
  and and_11 (and_11_out, multiplexer_1_out[0], multiplexer_1_out[1], multiplexer_1_out[2], ~multiplexer_1_out[3], multiplexer_1_out[4], multiplexer_1_out[5], ~multiplexer_1_out[6]);  // AND_Gate
  and and_12 (and_12_out, multiplexer_1_out[0], multiplexer_1_out[1], multiplexer_1_out[2], ~multiplexer_1_out[3], multiplexer_1_out[4], ~multiplexer_1_out[5], ~multiplexer_1_out[6]);  // AND_Gate
  and and_13 (and_13_out, multiplexer_1_out[0], multiplexer_1_out[1], multiplexer_1_out[2], multiplexer_1_out[3], ~multiplexer_1_out[4], multiplexer_1_out[5], multiplexer_1_out[6]);  // AND_Gate
  Multiplexer #(.width(25)) multiplexer_5 (
    .in0({1'b0, register_1_q}), .in1({multiplexer_15_out_2[0], multiplexer_15_out}), .out(multiplexer_5_out),
    .sel(or_4_out));
  not not_2 (not_2_out, multiplexer_5_out[24]);
  and and_14 (and_14_out, not_2_out, and_9_out);
  assign {controlled_buffer_2_out[17:8], controlled_buffer_1_out} = and_5_out ? {multiplexer_1_out[24:15], multiplexer_1_out[11:7]} : 15'bz;  // Controlled_Buffer controlled_buffer_3
  assign controlled_buffer_4_out = and_5_out ? 2'b00 : 2'bz;  // Controlled_Buffer controlled_buffer_4
  assign controlled_buffer_4_out = and_6_out ? 2'b00 : 2'bz;  // Controlled_Buffer controlled_buffer_5
  assign {controlled_buffer_6_out, controlled_buffer_1_out} = or_5_out ? multiplexer_1_out[31:7] : 25'bz;  // Controlled_Buffer controlled_buffer_6
  or or_5 (or_5_out, and_11_out, and_12_out);
  assign {controlled_buffer_7_out[20], controlled_buffer_7_out[10:1], controlled_buffer_7_out[11], controlled_buffer_7_out[19:12], controlled_buffer_1_out} = and_13_out ? multiplexer_1_out[31:7] : 25'bz;  // Controlled_Buffer controlled_buffer_7
  and and_15 (and_15_out, and_9_out, multiplexer_5_out[24]);
  Demultiplexer #(.width(24)) demultiplexer_1 (
    .out0({demultiplexer_1_out0_2, demultiplexer_1_out0}), .out1(demultiplexer_1_out1),
    .in(multiplexer_5_out[23:0]), .sel(multiplexer_5_out[24]));
  Multiplexer #(.width(2)) multiplexer_6 (
    .in0(2'b00), .in1(controlled_buffer_44_out), .out(multiplexer_6_out), .sel(and_9_out));
  and and_16 (and_16_out, ~multiplexer_1_out[12], ~multiplexer_1_out[13], ~multiplexer_1_out[14], and_5_out);  // AND_Gate
  and and_17 (and_17_out, ~multiplexer_1_out[12], ~multiplexer_1_out[13], multiplexer_1_out[14], and_5_out);  // AND_Gate
  and and_18 (and_18_out, ~multiplexer_1_out[12], multiplexer_1_out[13], multiplexer_1_out[14], and_5_out);  // AND_Gate
  and and_19 (and_19_out, multiplexer_1_out[12], multiplexer_1_out[13], multiplexer_1_out[14], and_5_out);
  and and_20 (and_20_out, multiplexer_1_out[12], ~multiplexer_1_out[13], ~multiplexer_1_out[14], and_5_out);  // AND_Gate
  and and_21 (and_21_out, multiplexer_1_out[12], ~multiplexer_1_out[13], multiplexer_1_out[14], and_5_out);  // AND_Gate
  and and_22 (and_22_out, ~multiplexer_1_out[12], multiplexer_1_out[13], ~multiplexer_1_out[14], and_5_out);  // AND_Gate
  and and_23 (and_23_out, multiplexer_1_out[12], multiplexer_1_out[13], ~multiplexer_1_out[14], and_5_out);  // AND_Gate
  assign {controlled_buffer_8_out, controlled_buffer_2_out[12:8], controlled_buffer_1_out} = or_6_out ? {multiplexer_1_out[31:15], multiplexer_1_out[11:7]} : 22'bz;  // Controlled_Buffer controlled_buffer_8
  or or_6 (or_6_out, and_6_out, and_7_out, and_8_out);
  and and_24 (and_24_out, multiplexer_1_out[12], ~multiplexer_1_out[13], ~multiplexer_1_out[14], and_6_out);  // AND_Gate
  and and_25 (and_25_out, multiplexer_1_out[12], ~multiplexer_1_out[13], multiplexer_1_out[14], and_6_out);  // AND_Gate
  assign {controlled_buffer_9_out, controlled_buffer_2_out[17:8]} = and_9_out ? {multiplexer_1_out[31:25], multiplexer_1_out[11:7], multiplexer_1_out[24:15]} : 22'bz;  // Controlled_Buffer controlled_buffer_9
  assign controlled_buffer_10_out = or_5_out ? {12{1'b0}} : 12'bz;  // Controlled_Buffer controlled_buffer_10
  assign controlled_buffer_4_out = and_11_out ? 2'b00 : 2'bz;  // Controlled_Buffer controlled_buffer_11
  not not_3 (not_3_out, CLK);
  Demultiplexer #(.select(3)) demultiplexer_2 (
    .out0(demultiplexer_2_out0), .out2(demultiplexer_2_out2), .out3(demultiplexer_2_out3), .in(not_3_out),
    .sel(demultiplexer_1_out1[4:2]));  // open: out1, out4, out5, out6, out7
  Demultiplexer #(.select(3)) demultiplexer_3 (
    .out0(demultiplexer_3_out0), .out1(demultiplexer_3_out1), .out4(demultiplexer_3_out4),
    .out5(demultiplexer_3_out5), .in(and_15_out), .sel(demultiplexer_1_out1[4:2]));  // open: out2, out3, out6, out7
  Demultiplexer #(.select(2)) demultiplexer_4 (
    .out0(demultiplexer_4_out0), .out1(demultiplexer_4_out1), .out2(demultiplexer_4_out2), .in(and_14_out),
    .sel(multiplexer_6_out));  // open: out3
  assign {bit_extender_2_out_2, bit_extender_2_out} = {{20{controlled_buffer_8_out[21]}}, controlled_buffer_8_out};  // Bit_Extender bit_extender_2
  assign bit_extender_3_out = {{11{controlled_buffer_2_out[24]}}, {controlled_buffer_2_out[24], controlled_buffer_2_out[0], controlled_buffer_2_out[23:18], controlled_buffer_2_out[4:1], 1'b0}};  // Bit_Extender bit_extender_3
  Bit_Extender #(.in_width(32), .out_width(7)) bit_extender_4 (
    .in({multiplexer_23_out_4, multiplexer_23_out_3, multiplexer_23_out_2, multiplexer_23_out}),
    .out(bit_extender_4_out));
  TTY #(.cols(38), .rows(16)) tty_1 (
    .data(bit_extender_4_out), .clk(demultiplexer_2_out0), .we(demultiplexer_3_out0),
    .clr(demultiplexer_3_out1));
  Demultiplexer #(.select(2)) demultiplexer_5 (
    .out0(demultiplexer_5_out0), .out1(demultiplexer_5_out1), .out2(demultiplexer_5_out2),
    .out3(demultiplexer_5_out3), .in(demultiplexer_4_out1), .sel(demultiplexer_1_out0));
  Demultiplexer #(.select(2)) demultiplexer_6 (
    .out0(demultiplexer_6_out0), .out1(demultiplexer_6_out1), .out2(demultiplexer_6_out2),
    .out3(demultiplexer_6_out3), .in(demultiplexer_4_out2), .sel(demultiplexer_1_out0));
  assign controlled_buffer_12_out = and_26_out ? 4'b0000 : 4'bz;  // Controlled_Buffer controlled_buffer_12
  and and_26 (and_26_out, and_16_out, ~multiplexer_1_out[25], ~multiplexer_1_out[26], ~multiplexer_1_out[27], ~multiplexer_1_out[28], ~multiplexer_1_out[29], ~multiplexer_1_out[30], ~multiplexer_1_out[31]);  // AND_Gate
  assign controlled_buffer_12_out = and_27_out ? 4'b0001 : 4'bz;  // Controlled_Buffer controlled_buffer_13
  and and_27 (and_27_out, and_16_out, ~multiplexer_1_out[25], ~multiplexer_1_out[26], ~multiplexer_1_out[27], ~multiplexer_1_out[28], ~multiplexer_1_out[29], multiplexer_1_out[30], ~multiplexer_1_out[31]);  // AND_Gate
  assign controlled_buffer_12_out = and_28_out ? 4'b0100 : 4'bz;  // Controlled_Buffer controlled_buffer_14
  and and_28 (and_28_out, and_17_out, ~multiplexer_1_out[25], ~multiplexer_1_out[26], ~multiplexer_1_out[27], ~multiplexer_1_out[28], ~multiplexer_1_out[29], ~multiplexer_1_out[30], ~multiplexer_1_out[31]);  // AND_Gate
  assign controlled_buffer_12_out = and_29_out ? 4'b0011 : 4'bz;  // Controlled_Buffer controlled_buffer_15
  and and_29 (and_29_out, and_18_out, ~multiplexer_1_out[25], ~multiplexer_1_out[26], ~multiplexer_1_out[27], ~multiplexer_1_out[28], ~multiplexer_1_out[29], ~multiplexer_1_out[30], ~multiplexer_1_out[31]);  // AND_Gate
  assign controlled_buffer_12_out = and_30_out ? 4'b0010 : 4'bz;  // Controlled_Buffer controlled_buffer_16
  and and_30 (and_30_out, and_19_out, ~multiplexer_1_out[25], ~multiplexer_1_out[26], ~multiplexer_1_out[27], ~multiplexer_1_out[28], ~multiplexer_1_out[29], ~multiplexer_1_out[30], ~multiplexer_1_out[31]);  // AND_Gate
  assign controlled_buffer_12_out = and_31_out ? 4'b0101 : 4'bz;  // Controlled_Buffer controlled_buffer_17
  and and_31 (and_31_out, and_20_out, ~multiplexer_1_out[25], ~multiplexer_1_out[26], ~multiplexer_1_out[27], ~multiplexer_1_out[28], ~multiplexer_1_out[29], ~multiplexer_1_out[30], ~multiplexer_1_out[31]);  // AND_Gate
  assign controlled_buffer_12_out = and_32_out ? 4'b0110 : 4'bz;  // Controlled_Buffer controlled_buffer_18
  and and_32 (and_32_out, and_21_out, ~multiplexer_1_out[25], ~multiplexer_1_out[26], ~multiplexer_1_out[27], ~multiplexer_1_out[28], ~multiplexer_1_out[29], ~multiplexer_1_out[30], ~multiplexer_1_out[31]);  // AND_Gate
  assign controlled_buffer_12_out = and_33_out ? 4'b0111 : 4'bz;  // Controlled_Buffer controlled_buffer_19
  and and_33 (and_33_out, and_21_out, ~multiplexer_1_out[25], ~multiplexer_1_out[26], ~multiplexer_1_out[27], ~multiplexer_1_out[28], ~multiplexer_1_out[29], multiplexer_1_out[30], ~multiplexer_1_out[31]);  // AND_Gate
  assign controlled_buffer_12_out = and_34_out ? 4'b1100 : 4'bz;  // Controlled_Buffer controlled_buffer_20
  and and_34 (and_34_out, and_22_out, ~multiplexer_1_out[25], ~multiplexer_1_out[26], ~multiplexer_1_out[27], ~multiplexer_1_out[28], ~multiplexer_1_out[29], ~multiplexer_1_out[30], ~multiplexer_1_out[31]);  // AND_Gate
  assign controlled_buffer_12_out = and_35_out ? 4'b1101 : 4'bz;  // Controlled_Buffer controlled_buffer_21
  and and_35 (and_35_out, and_23_out, ~multiplexer_1_out[25], ~multiplexer_1_out[26], ~multiplexer_1_out[27], ~multiplexer_1_out[28], ~multiplexer_1_out[29], ~multiplexer_1_out[30], ~multiplexer_1_out[31]);  // AND_Gate
  assign controlled_buffer_12_out = and_36_out ? 4'b0000 : 4'bz;  // Controlled_Buffer controlled_buffer_22
  and and_36 (and_36_out, ~multiplexer_1_out[12], ~multiplexer_1_out[13], ~multiplexer_1_out[14], and_6_out);  // AND_Gate
  assign controlled_buffer_12_out = and_37_out ? 4'b0100 : 4'bz;  // Controlled_Buffer controlled_buffer_23
  and and_37 (and_37_out, ~multiplexer_1_out[12], ~multiplexer_1_out[13], multiplexer_1_out[14], and_6_out);  // AND_Gate
  assign controlled_buffer_12_out = and_38_out ? 4'b0011 : 4'bz;  // Controlled_Buffer controlled_buffer_24
  and and_38 (and_38_out, ~multiplexer_1_out[12], multiplexer_1_out[13], multiplexer_1_out[14], and_6_out);  // AND_Gate
  assign controlled_buffer_12_out = and_39_out ? 4'b0010 : 4'bz;  // Controlled_Buffer controlled_buffer_25
  and and_39 (and_39_out, multiplexer_1_out[12], multiplexer_1_out[13], multiplexer_1_out[14], and_6_out);
  assign controlled_buffer_12_out = and_40_out ? 4'b1000 : 4'bz;  // Controlled_Buffer controlled_buffer_26
  and and_40 (and_40_out, ~multiplexer_1_out[12], multiplexer_1_out[13], ~multiplexer_1_out[14], and_6_out);  // AND_Gate
  assign controlled_buffer_12_out = and_41_out ? 4'b1001 : 4'bz;  // Controlled_Buffer controlled_buffer_27
  and and_41 (and_41_out, multiplexer_1_out[12], multiplexer_1_out[13], ~multiplexer_1_out[14], and_6_out);  // AND_Gate
  assign controlled_buffer_12_out = and_42_out ? 4'b0101 : 4'bz;  // Controlled_Buffer controlled_buffer_28
  and and_42 (and_42_out, and_24_out, ~multiplexer_1_out[25], ~multiplexer_1_out[26], ~multiplexer_1_out[27], ~multiplexer_1_out[28], ~multiplexer_1_out[29], ~multiplexer_1_out[30], ~multiplexer_1_out[31]);  // AND_Gate
  assign controlled_buffer_12_out = and_43_out ? 4'b0110 : 4'bz;  // Controlled_Buffer controlled_buffer_29
  and and_43 (and_43_out, and_25_out, ~multiplexer_1_out[25], ~multiplexer_1_out[26], ~multiplexer_1_out[27], ~multiplexer_1_out[28], ~multiplexer_1_out[29], ~multiplexer_1_out[30], ~multiplexer_1_out[31]);  // AND_Gate
  assign controlled_buffer_12_out = and_44_out ? 4'b0111 : 4'bz;  // Controlled_Buffer controlled_buffer_30
  and and_44 (and_44_out, and_25_out, ~multiplexer_1_out[25], ~multiplexer_1_out[26], ~multiplexer_1_out[27], ~multiplexer_1_out[28], ~multiplexer_1_out[29], multiplexer_1_out[30], ~multiplexer_1_out[31]);  // AND_Gate
  assign controlled_buffer_12_out = and_45_out ? 4'b0000 : 4'bz;  // Controlled_Buffer controlled_buffer_31
  and and_45 (and_45_out, ~multiplexer_1_out[12], ~multiplexer_1_out[13], ~multiplexer_1_out[14], and_7_out);  // AND_Gate
  assign controlled_buffer_32_out = and_45_out ? 3'b000 : 3'bz;  // Controlled_Buffer controlled_buffer_32
  assign controlled_buffer_12_out = and_46_out ? 4'b0000 : 4'bz;  // Controlled_Buffer controlled_buffer_33
  and and_46 (and_46_out, multiplexer_1_out[12], ~multiplexer_1_out[13], ~multiplexer_1_out[14], and_7_out);  // AND_Gate
  assign controlled_buffer_32_out = and_46_out ? 3'b001 : 3'bz;  // Controlled_Buffer controlled_buffer_34
  assign controlled_buffer_12_out = and_47_out ? 4'b0000 : 4'bz;  // Controlled_Buffer controlled_buffer_35
  and and_47 (and_47_out, ~multiplexer_1_out[12], multiplexer_1_out[13], ~multiplexer_1_out[14], and_7_out);  // AND_Gate
  assign controlled_buffer_32_out = and_47_out ? 3'b010 : 3'bz;  // Controlled_Buffer controlled_buffer_36
  assign controlled_buffer_12_out = and_48_out ? 4'b0000 : 4'bz;  // Controlled_Buffer controlled_buffer_37
  and and_48 (and_48_out, ~multiplexer_1_out[12], ~multiplexer_1_out[13], multiplexer_1_out[14], and_7_out);  // AND_Gate
  assign controlled_buffer_32_out = and_48_out ? 3'b011 : 3'bz;  // Controlled_Buffer controlled_buffer_38
  assign controlled_buffer_12_out = and_49_out ? 4'b0000 : 4'bz;  // Controlled_Buffer controlled_buffer_39
  and and_49 (and_49_out, multiplexer_1_out[12], ~multiplexer_1_out[13], multiplexer_1_out[14], and_7_out);  // AND_Gate
  assign controlled_buffer_32_out = and_49_out ? 3'b100 : 3'bz;  // Controlled_Buffer controlled_buffer_40
  assign controlled_buffer_12_out = and_50_out ? 4'b0000 : 4'bz;  // Controlled_Buffer controlled_buffer_41
  and and_50 (and_50_out, ~multiplexer_1_out[12], ~multiplexer_1_out[13], ~multiplexer_1_out[14], and_8_out);  // AND_Gate
  assign controlled_buffer_4_out = and_50_out ? 2'b10 : 2'bz;  // Controlled_Buffer controlled_buffer_42
  assign {bit_extender_2_out_2, bit_extender_2_out} = {{20{controlled_buffer_9_out[21]}}, controlled_buffer_9_out};  // Bit_Extender bit_extender_5
  assign controlled_buffer_12_out = and_51_out ? 4'b0000 : 4'bz;  // Controlled_Buffer controlled_buffer_43
  and and_51 (and_51_out, ~multiplexer_1_out[12], ~multiplexer_1_out[13], ~multiplexer_1_out[14], and_9_out);  // AND_Gate
  assign controlled_buffer_44_out = and_51_out ? 2'b10 : 2'bz;  // Controlled_Buffer controlled_buffer_44
  assign controlled_buffer_12_out = and_52_out ? 4'b0000 : 4'bz;  // Controlled_Buffer controlled_buffer_45
  and and_52 (and_52_out, multiplexer_1_out[12], ~multiplexer_1_out[13], ~multiplexer_1_out[14], and_9_out);  // AND_Gate
  assign controlled_buffer_44_out = and_52_out ? 2'b01 : 2'bz;  // Controlled_Buffer controlled_buffer_46
  assign controlled_buffer_12_out = and_53_out ? 4'b0000 : 4'bz;  // Controlled_Buffer controlled_buffer_47
  and and_53 (and_53_out, ~multiplexer_1_out[12], multiplexer_1_out[13], ~multiplexer_1_out[14], and_9_out);  // AND_Gate
  assign controlled_buffer_44_out = and_53_out ? 2'b00 : 2'bz;  // Controlled_Buffer controlled_buffer_48
  assign controlled_buffer_12_out = and_54_out ? 4'b1000 : 4'bz;  // Controlled_Buffer controlled_buffer_49
  and and_54 (and_54_out, ~controlled_buffer_2_out[5], ~controlled_buffer_2_out[6], ~controlled_buffer_2_out[7], and_10_out);  // AND_Gate
  assign controlled_buffer_12_out = and_55_out ? 4'b1001 : 4'bz;  // Controlled_Buffer controlled_buffer_50
  and and_55 (and_55_out, controlled_buffer_2_out[5], ~controlled_buffer_2_out[6], ~controlled_buffer_2_out[7], and_10_out);  // AND_Gate
  assign controlled_buffer_12_out = and_56_out ? 4'b1100 : 4'bz;  // Controlled_Buffer controlled_buffer_51
  and and_56 (and_56_out, ~controlled_buffer_2_out[5], ~controlled_buffer_2_out[6], controlled_buffer_2_out[7], and_10_out);  // AND_Gate
  assign controlled_buffer_12_out = and_57_out ? 4'b1010 : 4'bz;  // Controlled_Buffer controlled_buffer_52
  and and_57 (and_57_out, controlled_buffer_2_out[5], ~controlled_buffer_2_out[6], controlled_buffer_2_out[7], and_10_out);  // AND_Gate
  assign controlled_buffer_12_out = and_58_out ? 4'b1101 : 4'bz;  // Controlled_Buffer controlled_buffer_53
  and and_58 (and_58_out, ~controlled_buffer_2_out[5], controlled_buffer_2_out[6], controlled_buffer_2_out[7], and_10_out);  // AND_Gate
  assign controlled_buffer_12_out = and_59_out ? 4'b1011 : 4'bz;  // Controlled_Buffer controlled_buffer_54
  and and_59 (and_59_out, controlled_buffer_2_out[5], controlled_buffer_2_out[6], controlled_buffer_2_out[7], and_10_out);
  assign controlled_buffer_12_out = and_11_out ? 4'b0000 : 4'bz;  // Controlled_Buffer controlled_buffer_55
  assign {bit_extender_2_out_2, bit_extender_2_out} = and_11_out ? {32{1'b0}} : 32'bz;  // Controlled_Buffer controlled_buffer_56
  assign controlled_buffer_12_out = and_12_out ? 4'b0000 : 4'bz;  // Controlled_Buffer controlled_buffer_57
  assign controlled_buffer_4_out = and_12_out ? 2'b00 : 2'bz;  // Controlled_Buffer controlled_buffer_58
  assign controlled_buffer_12_out = and_13_out ? 4'b0000 : 4'bz;  // Controlled_Buffer controlled_buffer_59
  assign controlled_buffer_4_out = and_13_out ? 2'b10 : 2'bz;  // Controlled_Buffer controlled_buffer_60
  Bit_Extender #(.in_width(32), .out_width(22)) bit_extender_6 (
    .in({multiplexer_23_out_4, multiplexer_23_out_3, multiplexer_23_out_2, multiplexer_23_out}),
    .out(bit_extender_6_out));
  Adder #(.width(22)) adder_2 (.a(demultiplexer_1_out0_2), .b(22'h1), .out(adder_2_out));  // open: cin, cout
  assign controlled_buffer_4_out = and_7_out ? 2'b01 : 2'bz;  // Controlled_Buffer controlled_buffer_61
  assign bit_extender_3_out = {{3{controlled_buffer_7_out[20]}}, {controlled_buffer_7_out, 1'b0}};  // Bit_Extender bit_extender_7
  // RGB_Video #(.cursor("No Cursor")) rgb_video_1: pin names not known; wires that end beside it: demultiplexer_3_out5, demultiplexer_2_out3, demultiplexer_3_out4, bit_extender_6_out[6:0], bit_extender_6_out[13:7], bit_extender_6_out[21:14]
  Keyboard keyboard_1 (.clk(demultiplexer_2_out2), .avail(keyboard_1_avail), .data(keyboard_1_data));  // open: re, clr
  Multiplexer #(.select(2), .width(8)) multiplexer_7 (
    .in0(multiplexer_23_out), .in1(multiplexer_23_out_4), .in2(multiplexer_23_out_3),
    .in3(multiplexer_23_out_2), .out(multiplexer_7_out), .sel(demultiplexer_1_out0));
  Multiplexer #(.select(2), .width(8)) multiplexer_8 (
    .in0(multiplexer_23_out_2), .in1(multiplexer_23_out), .in2(multiplexer_23_out_4),
    .in3(multiplexer_23_out_3), .out(multiplexer_8_out), .sel(demultiplexer_1_out0));
  Multiplexer #(.select(2), .width(8)) multiplexer_9 (
    .in0(multiplexer_23_out_3), .in1(multiplexer_23_out_2), .in2(multiplexer_23_out),
    .in3(multiplexer_23_out_4), .out(multiplexer_9_out), .sel(demultiplexer_1_out0));
  Multiplexer #(.select(2), .width(8)) multiplexer_10 (
    .in0(multiplexer_23_out_4), .in1(multiplexer_23_out_3), .in2(multiplexer_23_out_2),
    .in3(multiplexer_23_out), .out(multiplexer_10_out), .sel(demultiplexer_1_out0));
  Multiplexer #(.select(2), .width(22)) multiplexer_11 (
    .in0(demultiplexer_1_out0_2), .in1(adder_2_out), .in2(adder_2_out), .in3(adder_2_out),
    .out(multiplexer_11_out), .sel(demultiplexer_1_out0));
  Multiplexer #(.select(2), .width(22)) multiplexer_12 (
    .in0(demultiplexer_1_out0_2), .in1(demultiplexer_1_out0_2), .in2(adder_2_out), .in3(adder_2_out),
    .out(multiplexer_12_out), .sel(demultiplexer_1_out0));
  Multiplexer #(.select(2), .width(22)) multiplexer_13 (
    .in0(demultiplexer_1_out0_2), .in1(demultiplexer_1_out0_2), .in2(demultiplexer_1_out0_2),
    .in3(adder_2_out), .out(multiplexer_13_out), .sel(demultiplexer_1_out0));
  assign bit_extender_8_out = {{25{1'b0}}, keyboard_1_data};  // Bit_Extender bit_extender_8
  assign bit_extender_9_out = {{31{1'b0}}, keyboard_1_avail};  // Bit_Extender bit_extender_9
  or or_7 (or_7_out, demultiplexer_4_out0, demultiplexer_5_out0, demultiplexer_5_out3, demultiplexer_6_out0);
  or or_8 (or_8_out, demultiplexer_4_out0, demultiplexer_5_out0, demultiplexer_5_out1, demultiplexer_6_out1);
  or or_9 (or_9_out, demultiplexer_4_out0, demultiplexer_5_out1, demultiplexer_5_out2, demultiplexer_6_out2);
  or or_10 (or_10_out, demultiplexer_4_out0, demultiplexer_5_out2, demultiplexer_5_out3, demultiplexer_6_out3);
  assign {bit_extender_2_out_2, bit_extender_2_out} = and_12_out ? {{8{1'b0}}, subtractor_2_out} : 32'bz;  // Controlled_Buffer controlled_buffer_62
  Multiplexer #(.select(3), .width(32)) multiplexer_14 (
    .in2(bit_extender_8_out), .in3(bit_extender_9_out), .out(multiplexer_14_out),
    .sel(demultiplexer_1_out1[4:2]));  // open: in0, in1, in4, in5, in6, in7
  RAM #(.addrWidth(22), .asyncread("true"), .trigger("falling")) ram_1 (
    .addr(multiplexer_11_out), .we(or_7_out), .oe(1'b1), .clk(CLK), .din(multiplexer_7_out), .dout(ram_1_dout));
  RAM #(.addrWidth(22), .asyncread("true"), .trigger("falling")) ram_2 (
    .addr(multiplexer_12_out), .we(or_8_out), .oe(1'b1), .clk(CLK), .din(multiplexer_8_out), .dout(ram_2_dout));
  RAM #(.addrWidth(22), .asyncread("true"), .trigger("falling")) ram_3 (
    .addr(multiplexer_13_out), .we(or_9_out), .oe(1'b1), .clk(CLK), .din(multiplexer_9_out), .dout(ram_3_dout));
  RAM #(.addrWidth(22), .asyncread("true"), .trigger("falling")) ram_4 (
    .addr(demultiplexer_1_out0_2), .we(or_10_out), .oe(1'b1), .clk(CLK), .din(multiplexer_10_out),
    .dout(ram_4_dout));
  assign controlled_buffer_63_out = multiplexer_5_out[24] ? multiplexer_14_out : 32'bz;  // Controlled_Buffer controlled_buffer_63
  Adder #(.width(32)) adder_3 (
    .a({controlled_buffer_6_out, controlled_buffer_10_out}), .b({bit_extender_2_out_2, bit_extender_2_out}),
    .out(adder_3_out));  // open: cin, cout
  Subtractor #(.width(32)) subtractor_3 (
    .a({controlled_buffer_6_out, controlled_buffer_10_out}), .b({bit_extender_2_out_2, bit_extender_2_out}),
    .out(subtractor_3_out));  // open: bin, bout
  assign and_60_out = {controlled_buffer_6_out, controlled_buffer_10_out} & {bit_extender_2_out_2, bit_extender_2_out};  // AND_Gate and_60, 32 bits wide
  assign or_11_out = {controlled_buffer_6_out, controlled_buffer_10_out} | {bit_extender_2_out_2, bit_extender_2_out};  // OR_Gate or_11, 32 bits wide
  assign xor_1_out = {controlled_buffer_6_out, controlled_buffer_10_out} ^ {bit_extender_2_out_2, bit_extender_2_out};  // XOR_Gate xor_1, 32 bits wide
  Shifter #(.width(32)) shifter_1 (
    .in({controlled_buffer_6_out, controlled_buffer_10_out}), .\dist (bit_extender_2_out), .out(shifter_1_out));
  Shifter #(.shift("lr"), .width(32)) shifter_2 (
    .in({controlled_buffer_6_out, controlled_buffer_10_out}), .\dist (bit_extender_2_out), .out(shifter_2_out));
  Shifter #(.shift("ar"), .width(32)) shifter_3 (
    .in({controlled_buffer_6_out, controlled_buffer_10_out}), .\dist (bit_extender_2_out), .out(shifter_3_out));
  or or_12 (or_12_out, comparator_1_gt, comparator_1_eq);
  not not_4 (not_4_out, comparator_1_eq);
  Comparator #(.width(32)) comparator_1 (
    .a({controlled_buffer_6_out, controlled_buffer_10_out}), .b({bit_extender_2_out_2, bit_extender_2_out}),
    .gt(comparator_1_gt), .eq(comparator_1_eq), .lt(comparator_1_lt));
  or or_13 (or_13_out, comparator_2_gt, comparator_2_eq);
  Comparator #(.mode("unsigned"), .width(32)) comparator_2 (
    .a({controlled_buffer_6_out, controlled_buffer_10_out}), .b({bit_extender_2_out_2, bit_extender_2_out}),
    .gt(comparator_2_gt), .eq(comparator_2_eq), .lt(comparator_2_lt));
  assign bit_extender_10_out = {{31{1'b0}}, or_12_out};  // Bit_Extender bit_extender_10
  assign bit_extender_11_out = {{31{1'b0}}, not_4_out};  // Bit_Extender bit_extender_11
  assign bit_extender_12_out = {{31{1'b0}}, comparator_1_eq};  // Bit_Extender bit_extender_12
  assign bit_extender_13_out = {{31{1'b0}}, comparator_1_lt};  // Bit_Extender bit_extender_13
  assign bit_extender_14_out = {{31{1'b0}}, or_13_out};  // Bit_Extender bit_extender_14
  assign bit_extender_15_out = {{31{1'b0}}, comparator_2_lt};  // Bit_Extender bit_extender_15
  or or_14 (or_14_out, and_9_out, or_5_out);
  Multiplexer #(.select(4), .width(32)) multiplexer_15 (
    .in0(adder_3_out), .in1(subtractor_3_out), .in2(and_60_out), .in3(or_11_out), .in4(xor_1_out),
    .in5(shifter_1_out), .in6(shifter_2_out), .in7(shifter_3_out), .in8(bit_extender_12_out),
    .in9(bit_extender_11_out), .in10(bit_extender_10_out), .in11(bit_extender_14_out),
    .in12(bit_extender_13_out), .in13(bit_extender_15_out), .out({multiplexer_15_out_2, multiplexer_15_out}),
    .sel(controlled_buffer_12_out));  // open: in14, in15
  Multiplexer #(.select(2), .width(8)) multiplexer_16 (
    .in0(ram_1_dout), .in1(ram_2_dout), .in2(ram_3_dout), .in3(ram_4_dout), .out(multiplexer_16_out),
    .sel(demultiplexer_1_out0));
  Multiplexer #(.select(2), .width(8)) multiplexer_17 (
    .in0(ram_2_dout), .in1(ram_3_dout), .in2(ram_4_dout), .in3(ram_1_dout), .out(multiplexer_17_out),
    .sel(demultiplexer_1_out0));
  Multiplexer #(.select(2), .width(8)) multiplexer_18 (
    .in0(ram_3_dout), .in1(ram_4_dout), .in2(ram_1_dout), .in3(ram_2_dout), .out(multiplexer_18_out),
    .sel(demultiplexer_1_out0));
  Multiplexer #(.select(2), .width(8)) multiplexer_19 (
    .in0(ram_4_dout), .in1(ram_1_dout), .in2(ram_2_dout), .in3(ram_3_dout), .out(multiplexer_19_out),
    .sel(demultiplexer_1_out0));
  Register #(.width(32)) register_2 (.D(controlled_buffer_63_out), .clk(CLK), .Q(RAM_OUT), .clr(in_2));  // open: en
  assign bit_extender_16_out = {{24{controlled_buffer_63_out[7]}}, controlled_buffer_63_out[7:0]};  // Bit_Extender bit_extender_16
  assign bit_extender_17_out = {{16{controlled_buffer_63_out[15]}}, controlled_buffer_63_out[15:0]};  // Bit_Extender bit_extender_17
  assign bit_extender_18_out = {{24{1'b0}}, controlled_buffer_63_out[7:0]};  // Bit_Extender bit_extender_18
  assign bit_extender_19_out = {{16{1'b0}}, controlled_buffer_63_out[15:0]};  // Bit_Extender bit_extender_19
  Multiplexer #(.select(3), .width(32)) multiplexer_20 (
    .in0(bit_extender_16_out), .in1(bit_extender_17_out), .in2(controlled_buffer_63_out),
    .in3(bit_extender_18_out), .in4(bit_extender_19_out), .out(multiplexer_20_out),
    .sel(controlled_buffer_32_out));  // open: in5, in6, in7
  assign controlled_buffer_63_out = not_2_out ? {multiplexer_19_out, multiplexer_18_out, multiplexer_17_out, multiplexer_16_out} : 32'bz;  // Controlled_Buffer controlled_buffer_64
  Multiplexer #(.select(2), .width(32)) multiplexer_21 (
    .in0({multiplexer_15_out_2, multiplexer_15_out}), .in1(multiplexer_20_out),
    .in2({{8{1'b0}}, register_1_q}), .out(multiplexer_21_out), .sel(controlled_buffer_4_out));  // open: in3
  Demultiplexer #(.select(5)) demultiplexer_7 (
    .out1(demultiplexer_7_out1), .out2(demultiplexer_7_out2), .out3(demultiplexer_7_out3),
    .out4(demultiplexer_7_out4), .out5(demultiplexer_7_out5), .out6(demultiplexer_7_out6),
    .out7(demultiplexer_7_out7), .out8(demultiplexer_7_out8), .out9(demultiplexer_7_out9),
    .out10(demultiplexer_7_out10), .out11(demultiplexer_7_out11), .out12(demultiplexer_7_out12),
    .out13(demultiplexer_7_out13), .out14(demultiplexer_7_out14), .out15(demultiplexer_7_out15),
    .out16(demultiplexer_7_out16), .out17(demultiplexer_7_out17), .out18(demultiplexer_7_out18),
    .out19(demultiplexer_7_out19), .out20(demultiplexer_7_out20), .out21(demultiplexer_7_out21),
    .out22(demultiplexer_7_out22), .out23(demultiplexer_7_out23), .out24(demultiplexer_7_out24),
    .out25(demultiplexer_7_out25), .out26(demultiplexer_7_out26), .out27(demultiplexer_7_out27),
    .out28(demultiplexer_7_out28), .out29(demultiplexer_7_out29), .out30(demultiplexer_7_out30),
    .out31(demultiplexer_7_out31), .in(1'b1), .sel(controlled_buffer_1_out));  // open: out0
  not not_5 (not_5_out, CLK);
  Register #(.width(32)) x31 (
    .D(multiplexer_21_out), .en(demultiplexer_7_out31), .clk(not_5_out), .Q(x31_q));  // open: clr
  Register #(.width(32)) x30 (
    .D(multiplexer_21_out), .en(demultiplexer_7_out30), .clk(not_5_out), .Q(x30_q));  // open: clr
  Register #(.width(32)) x29 (
    .D(multiplexer_21_out), .en(demultiplexer_7_out29), .clk(not_5_out), .Q(x29_q));  // open: clr
  Register #(.width(32)) x28 (
    .D(multiplexer_21_out), .en(demultiplexer_7_out28), .clk(not_5_out), .Q(x28_q));  // open: clr
  Register #(.width(32)) x27 (
    .D(multiplexer_21_out), .en(demultiplexer_7_out27), .clk(not_5_out), .Q(x27_q));  // open: clr
  Register #(.width(32)) x26 (
    .D(multiplexer_21_out), .en(demultiplexer_7_out26), .clk(not_5_out), .Q(x26_q));  // open: clr
  Register #(.width(32)) x25 (
    .D(multiplexer_21_out), .en(demultiplexer_7_out25), .clk(not_5_out), .Q(x25_q));  // open: clr
  Register #(.width(32)) x24 (
    .D(multiplexer_21_out), .en(demultiplexer_7_out24), .clk(not_5_out), .Q(x24_q));  // open: clr
  Register #(.width(32)) x23 (
    .D(multiplexer_21_out), .en(demultiplexer_7_out23), .clk(not_5_out), .Q(x23_q));  // open: clr
  Register #(.width(32)) x22 (
    .D(multiplexer_21_out), .en(demultiplexer_7_out22), .clk(not_5_out), .Q(x22_q));  // open: clr
  Register #(.width(32)) x21 (
    .D(multiplexer_21_out), .en(demultiplexer_7_out21), .clk(not_5_out), .Q(x21_q));  // open: clr
  Register #(.width(32)) x20 (
    .D(multiplexer_21_out), .en(demultiplexer_7_out20), .clk(not_5_out), .Q(x20_q));  // open: clr
  Register #(.width(32)) x19 (
    .D(multiplexer_21_out), .en(demultiplexer_7_out19), .clk(not_5_out), .Q(x19_q));  // open: clr
  Register #(.width(32)) x18 (
    .D(multiplexer_21_out), .en(demultiplexer_7_out18), .clk(not_5_out), .Q(x18_q));  // open: clr
  Register #(.width(32)) x17 (
    .D(multiplexer_21_out), .en(demultiplexer_7_out17), .clk(not_5_out), .Q(x17_q));  // open: clr
  Register #(.width(32)) x16 (
    .D(multiplexer_21_out), .en(demultiplexer_7_out16), .clk(not_5_out), .Q(x16_q));  // open: clr
  Register #(.width(32)) x15 (
    .D(multiplexer_21_out), .en(demultiplexer_7_out15), .clk(not_5_out), .Q(x15_q));  // open: clr
  Register #(.width(32)) x14 (
    .D(multiplexer_21_out), .en(demultiplexer_7_out14), .clk(not_5_out), .Q(x14_q));  // open: clr
  Register #(.width(32)) x13 (
    .D(multiplexer_21_out), .en(demultiplexer_7_out13), .clk(not_5_out), .Q(x13_q));  // open: clr
  Register #(.width(32)) x12 (
    .D(multiplexer_21_out), .en(demultiplexer_7_out12), .clk(not_5_out), .Q(x12_q));  // open: clr
  Register #(.width(32)) x11 (
    .D(multiplexer_21_out), .en(demultiplexer_7_out11), .clk(not_5_out), .Q(x11_q));  // open: clr
  Register #(.width(32)) x10 (
    .D(multiplexer_21_out), .en(demultiplexer_7_out10), .clk(not_5_out), .Q(x10_q));  // open: clr
  Register #(.width(32)) x9 (
    .D(multiplexer_21_out), .en(demultiplexer_7_out9), .clk(not_5_out), .Q(x9_q));  // open: clr
  Register #(.width(32)) x8 (
    .D(multiplexer_21_out), .en(demultiplexer_7_out8), .clk(not_5_out), .Q(x8_q));  // open: clr
  Register #(.width(32)) x7 (
    .D(multiplexer_21_out), .en(demultiplexer_7_out7), .clk(not_5_out), .Q(x7_q));  // open: clr
  Register #(.width(32)) x6 (
    .D(multiplexer_21_out), .en(demultiplexer_7_out6), .clk(not_5_out), .Q(x6_q));  // open: clr
  Register #(.width(32)) x5 (
    .D(multiplexer_21_out), .en(demultiplexer_7_out5), .clk(not_5_out), .Q(x5_q));  // open: clr
  Register #(.width(32)) x4 (
    .D(multiplexer_21_out), .en(demultiplexer_7_out4), .clk(not_5_out), .Q(x4_q));  // open: clr
  Register #(.width(32)) x3 (
    .D(multiplexer_21_out), .en(demultiplexer_7_out3), .clk(not_5_out), .Q(x3_q));  // open: clr
  Register #(.width(32)) x2 (
    .D(multiplexer_21_out), .en(demultiplexer_7_out2), .clk(not_5_out), .Q(x2_q));  // open: clr
  Register #(.width(32)) x1 (
    .D(multiplexer_21_out), .en(demultiplexer_7_out1), .clk(not_5_out), .Q(x1_q));  // open: clr
  not not_6 (not_6_out, or_5_out);
  Multiplexer #(.select(5), .width(32)) multiplexer_22 (
    .in0({32{1'b0}}), .in1(x1_q), .in2(x2_q), .in3(x3_q), .in4(x4_q), .in5(x5_q), .in6(x6_q), .in7(x7_q),
    .in8(x8_q), .in9(x9_q), .in10(x10_q), .in11(x11_q), .in12(x12_q), .in13(x13_q), .in14(x14_q),
    .in15(x15_q), .in16(x16_q), .in17(x17_q), .in18(x18_q), .in19(x19_q), .in20(x20_q), .in21(x21_q),
    .in22(x22_q), .in23(x23_q), .in24(x24_q), .in25(x25_q), .in26(x26_q), .in27(x27_q), .in28(x28_q),
    .in29(x29_q), .in30(x30_q), .in31(x31_q), .out(multiplexer_22_out), .sel(controlled_buffer_2_out[12:8]));
  assign {controlled_buffer_6_out, controlled_buffer_10_out} = not_6_out ? multiplexer_22_out : 32'bz;  // Controlled_Buffer controlled_buffer_65
  not not_7 (not_7_out, or_14_out);
  Multiplexer #(.select(5), .width(32)) multiplexer_23 (
    .in0({32{1'b0}}), .in1(x1_q), .in2(x2_q), .in3(x3_q), .in4(x4_q), .in5(x5_q), .in6(x6_q), .in7(x7_q),
    .in8(x8_q), .in9(x9_q), .in10(x10_q), .in11(x11_q), .in12(x12_q), .in13(x13_q), .in14(x14_q),
    .in15(x15_q), .in16(x16_q), .in17(x17_q), .in18(x18_q), .in19(x19_q), .in20(x20_q), .in21(x21_q),
    .in22(x22_q), .in23(x23_q), .in24(x24_q), .in25(x25_q), .in26(x26_q), .in27(x27_q), .in28(x28_q),
    .in29(x29_q), .in30(x30_q), .in31(x31_q),
    .out({multiplexer_23_out_4, multiplexer_23_out_3, multiplexer_23_out_2, multiplexer_23_out}),
    .sel(controlled_buffer_2_out[17:13]));
  assign {bit_extender_2_out_2, bit_extender_2_out} = not_7_out ? {multiplexer_23_out_4, multiplexer_23_out_3, multiplexer_23_out_2, multiplexer_23_out} : 32'bz;  // Controlled_Buffer controlled_buffer_66
endmodule
